// Logisim project e32.circ as structural Verilog: 10 circuits, main circuit main
module main (
);

  wire and_1_out, and_2_out, and_3_out, and_4_out, and_5_out, and_6_out, and_7_out, and_8_out, and_9_out,
       and_10_out, and_11_out, CClock, comparator_1_eq, comparator_1_gt, isADD, isDIV, isJMP, isJMPG, isJMPZ,
       isLOAD, isMOV, isMUL, isRAM0, isRAM1, isRAM_READ, isRAM_WRITE, isSCREEN_CLEAR, isSCREEN_DRAW, isSTORE,
       isSUB, or_1_out, or_2_out, or_3_out, or_4_out, or_6_out, or_7_out, or_8_out, or_9_out, or_10_out,
       or_11_out, or_13_out, PC_EQUAL_0, PC_EQUAL_GREAER_1, RegACCEnabled, RegAEnabled, RegBEnabled,
       RegCEnabled, RegDEnabled, RegEEnabled;
  wire [2:0] priority_encoder_1_out, priority_encoder_2_out;
  wire [7:0] adder_2_out, divider_1_out, IncrementedPCValue, multiplexer_1_out, multiplexer_3_out,
       multiplexer_4_out, multiplexer_5_out, multiplexer_6_out, multiplexer_7_out, multiplexer_8_out,
       multiplier_1_out, PCValue, RAM_0_READ, RAM_1_READ, subtractor_1_out, ValueLoad, ValueLoadACC,
       ValueRegA, ValueRegACC, ValueRegB, ValueRegC, ValueRegD, ValueRegE;

  Clock clock_1 (.out(CClock));
  Adder adder_1 (.a(PCValue), .b(8'h1), .out(IncrementedPCValue));  // open: cin, cout
  or or_1 (or_1_out, isLOAD, isADD);
  InstructionDecoder instructiondecoder_1 (
    .Opcode(8'hd), .isMOV(isMOV), .isJMP(isJMP), .isADD(isADD), .isSUB(isSUB), .isMUL(isMUL), .isDIV(isDIV),
    .isLOAD(isLOAD), .isSTORE(isSTORE), .isJMPG(isJMPG), .isJMPZ(isJMPZ), .isRAM_WRITE(isRAM_WRITE),
    .isRAM_READ(isRAM_READ), .isSCREEN_CLEAR(isSCREEN_CLEAR), .isSCREEN_DRAW(isSCREEN_DRAW));
  or or_2 (or_2_out, or_1_out, isMUL);
  RegEnabledDecoder regenableddecoder_1 (
    .isMOV(isMOV), .isADD(isADD), .isSUB(isSUB), .isMUL(isMUL), .isDIV(isDIV), .isLOAD(isLOAD),
    .isSTORE(isSTORE), .Operand1(8'h3), .RegAEnabled(RegAEnabled), .RegBEnabled(RegBEnabled),
    .RegCEnabled(RegCEnabled), .RegDEnabled(RegDEnabled), .RegEEnabled(RegEEnabled));
  or or_3 (or_3_out, or_2_out, isDIV);
  or or_4 (or_4_out, or_3_out, isSUB);
  or or_5 (RegACCEnabled, or_4_out, isRAM_READ);
  Priority_Encoder priority_encoder_1 (
    .in0(RegAEnabled), .in1(RegBEnabled), .in2(RegCEnabled), .in3(RegDEnabled), .in4(RegEEnabled),
    .out(priority_encoder_1_out));  // open: in5, in6, in7, en_in, gs, en_out
  or or_6 (or_6_out, isMOV, isSTORE);
  or or_7 (or_7_out, isMOV, isSTORE);
  or or_8 (or_8_out, isMOV, isSTORE);
  Multiplexer #(.width(8)) multiplexer_1 (.in0({8{1'b1}}), .in1(ValueRegACC), .out(multiplexer_1_out), .sel(isSTORE));
  or or_9 (or_9_out, isMOV, isSTORE);
  or or_10 (or_10_out, isMOV, isSTORE);
  Multiplexer #(.select(3), .width(8)) multiplexer_2 (
    .in0(ValueRegA), .in1(ValueRegB), .in2(ValueRegC), .in3(ValueRegD), .in4(ValueRegE), .out(ValueLoad),
    .sel(priority_encoder_1_out));  // open: in5, in6, in7
  Comparator comparator_1 (.a(ValueRegACC), .b(8'h1), .gt(comparator_1_gt), .eq(comparator_1_eq));  // open: lt
  Comparator comparator_2 (.a(ValueRegACC), .b({8{1'b0}}), .eq(PC_EQUAL_0));  // open: gt, lt
  Multiplexer #(.width(8)) multiplexer_3 (
    .in0(IncrementedPCValue), .in1(8'h3), .out(multiplexer_3_out), .sel(or_11_out));
  or or_11 (or_11_out, isJMP, or_13_out);
  and and_1 (and_1_out, PC_EQUAL_GREAER_1, isJMPG);
  Multiplexer #(.width(8)) multiplexer_4 (.in0({8{1'b1}}), .in1(ValueRegACC), .out(multiplexer_4_out), .sel(isSTORE));
  Multiplexer #(.width(8)) multiplexer_5 (.in0({8{1'b1}}), .in1(ValueRegACC), .out(multiplexer_5_out), .sel(isSTORE));
  Multiplexer #(.width(8)) multiplexer_6 (.in0({8{1'b1}}), .in1(ValueRegACC), .out(multiplexer_6_out), .sel(isSTORE));
  Multiplexer #(.width(8)) multiplexer_7 (.in0({8{1'b1}}), .in1(ValueRegACC), .out(multiplexer_7_out), .sel(isSTORE));
  or or_12 (PC_EQUAL_GREAER_1, comparator_1_gt, comparator_1_eq);
  Register PC (.D(multiplexer_3_out), .en(CClock), .clk(CClock), .Q(PCValue));  // open: clr
  or or_13 (or_13_out, and_1_out, and_7_out);
  and and_2 (and_2_out, or_6_out, RegAEnabled);
  and and_3 (and_3_out, or_7_out, RegBEnabled);
  and and_4 (and_4_out, or_8_out, RegCEnabled);
  and and_5 (and_5_out, or_9_out, RegDEnabled);
  and and_6 (and_6_out, or_10_out, RegEEnabled);
  and and_7 (and_7_out, PC_EQUAL_0, isJMPZ);
  Register RegA (.D(multiplexer_4_out), .en(and_2_out), .clk(CClock), .Q(ValueRegA));  // open: clr
  Register RegB (.D(multiplexer_5_out), .en(and_3_out), .clk(CClock), .Q(ValueRegB));  // open: clr
  Register RegC (.D(multiplexer_6_out), .en(and_4_out), .clk(CClock), .Q(ValueRegC));  // open: clr
  Register RegD (.D(multiplexer_1_out), .en(and_5_out), .clk(CClock), .Q(ValueRegD));  // open: clr
  Register RegE (.D(multiplexer_7_out), .en(and_6_out), .clk(CClock), .Q(ValueRegE));  // open: clr
  Register ACC (.D(ValueLoadACC), .en(RegACCEnabled), .clk(CClock), .Q(ValueRegACC));  // open: clr
  Adder adder_2 (.a(ValueLoad), .b({8{1'b1}}), .out(adder_2_out));  // open: cin, cout
  Subtractor subtractor_1 (.a(ValueLoad), .b({8{1'b1}}), .out(subtractor_1_out));  // open: bin, bout
  Multiplier multiplier_1 (.a(ValueLoad), .b({8{1'b1}}), .out(multiplier_1_out));  // open: cin, cout
  Divider divider_1 (.a(ValueLoad), .b({8{1'b1}}), .out(divider_1_out));  // open: upper, rem
  Multiplexer #(.width(8)) multiplexer_8 (.in0(RAM_0_READ), .in1(RAM_1_READ), .out(multiplexer_8_out), .sel(isRAM1));
  Multiplexer #(.select(3), .width(8)) multiplexer_9 (
    .in0({8{1'b1}}), .in1(adder_2_out), .in2(subtractor_1_out), .in3(multiplier_1_out), .in4(divider_1_out),
    .in5(ValueLoad), .in6(multiplexer_8_out), .out(ValueLoadACC), .sel(priority_encoder_2_out));  // open: in7
  Comparator #(.mode("unsigned")) comparator_3 (.a({8{1'b1}}), .b({8{1'b0}}), .eq(isRAM0));  // open: gt, lt
  Comparator #(.mode("unsigned")) comparator_4 (.a({8{1'b1}}), .b(8'h1), .eq(isRAM1));  // open: gt, lt
  and and_8 (and_8_out, isRAM0, isRAM_WRITE);
  and and_9 (and_9_out, isRAM0, isRAM_READ);
  and and_10 (and_10_out, isRAM1, isRAM_WRITE);
  and and_11 (and_11_out, isRAM1, isRAM_READ);
  // RGB_Video #(.height(256), .scale(1), .width(256)) rgb_video_1: pin names not known; wires that end beside it: isSCREEN_CLEAR, CClock, isSCREEN_DRAW, ValueRegD, ValueRegE, {ValueRegA, ValueRegB, ValueRegC}
  RAM ram_1 (.addr(8'h3), .we(and_8_out), .oe(and_9_out), .clk(CClock), .din(ValueRegACC), .dout(RAM_0_READ));
  RAM ram_2 (.addr(8'h3), .we(and_10_out), .oe(and_11_out), .clk(CClock), .din(ValueRegACC), .dout(RAM_1_READ));
  Priority_Encoder priority_encoder_2 (
    .in0(isMOV), .in1(isADD), .in2(isSUB), .in3(isMUL), .in4(isDIV), .in5(isLOAD), .in6(isRAM_READ),
    .out(priority_encoder_2_out));  // open: in7, en_in, gs, en_out

  // Notes on the sheet:
  //   DISPLAY
  //   .... Ram Index (256)
  //   RAM Index (0)
  //   Ram Index (1)
  //   R
  //   G
  //   B
endmodule

module InstructionDecoder (
  input  [7:0] Opcode,
  output isMOV,
  output isJMP,
  output isADD,
  output isSUB,
  output isMUL,
  output isDIV,
  output isLOAD,
  output isSTORE,
  output isJMPG,
  output isJMPZ,
  output isRAM_WRITE,
  output isRAM_READ,
  output isSCREEN_CLEAR,
  output isSCREEN_DRAW
);

  Comparator comparator_1 (.a(Opcode), .b({8{1'b0}}), .eq(isMOV));  // open: gt, lt
  Comparator comparator_2 (.a(Opcode), .b(8'h1), .eq(isJMP));  // open: gt, lt
  Comparator comparator_3 (.a(Opcode), .b(8'h2), .eq(isADD));  // open: gt, lt
  Comparator comparator_4 (.a(Opcode), .b(8'h3), .eq(isSUB));  // open: gt, lt
  Comparator comparator_5 (.a(Opcode), .b(8'h4), .eq(isMUL));  // open: gt, lt
  Comparator comparator_6 (.a(Opcode), .b(8'h5), .eq(isDIV));  // open: gt, lt
  Comparator comparator_7 (.a(Opcode), .b(8'h6), .eq(isLOAD));  // open: gt, lt
  Comparator comparator_8 (.a(Opcode), .b(8'h7), .eq(isSTORE));  // open: gt, lt
  Comparator comparator_9 (.a(Opcode), .b(8'h8), .eq(isJMPG));  // open: gt, lt
  Comparator comparator_10 (.a(Opcode), .b(8'h9), .eq(isJMPZ));  // open: gt, lt
  Comparator comparator_11 (.a(Opcode), .b(8'ha), .eq(isRAM_WRITE));  // open: gt, lt
  Comparator comparator_12 (.a(Opcode), .b(8'hb), .eq(isRAM_READ));  // open: gt, lt
  Comparator comparator_13 (.a(Opcode), .b(8'hc), .eq(isSCREEN_CLEAR));  // open: gt, lt
  Comparator comparator_14 (.a(Opcode), .b(8'hd), .eq(isSCREEN_DRAW));  // open: gt, lt
endmodule

module MOVRegDecoder (
  input  isMOV,
  input  [7:0] Operand1,
  output isMOVA,
  output isMOVB,
  output isMOVC,
  output isMOVD,
  output isMOVE
);

  wire comparator_1_eq, comparator_2_eq, comparator_3_eq, comparator_4_eq, comparator_5_eq;

  Comparator comparator_1 (.a(Operand1), .b(8'h1), .eq(comparator_1_eq));  // open: gt, lt
  Comparator comparator_2 (.a(Operand1), .b(8'h2), .eq(comparator_2_eq));  // open: gt, lt
  Comparator comparator_3 (.a(Operand1), .b(8'h3), .eq(comparator_3_eq));  // open: gt, lt
  Comparator comparator_4 (.a(Operand1), .b(8'h4), .eq(comparator_4_eq));  // open: gt, lt
  Comparator comparator_5 (.a(Operand1), .b(8'h5), .eq(comparator_5_eq));  // open: gt, lt
  and and_1 (isMOVA, isMOV, comparator_1_eq);
  and and_2 (isMOVB, isMOV, comparator_2_eq);
  and and_3 (isMOVC, isMOV, comparator_3_eq);
  and and_4 (isMOVD, isMOV, comparator_4_eq);
  and and_5 (isMOVE, isMOV, comparator_5_eq);
endmodule

module ADDRegDecoder (
  input  isADD,
  input  [7:0] Operand1,
  output isADDA,
  output isADDB,
  output isADDC,
  output isADDD,
  output isADDE
);

  wire comparator_1_eq, comparator_2_eq, comparator_3_eq, comparator_4_eq, comparator_5_eq;

  Comparator comparator_1 (.a(Operand1), .b(8'h1), .eq(comparator_1_eq));  // open: gt, lt
  Comparator comparator_2 (.a(Operand1), .b(8'h2), .eq(comparator_2_eq));  // open: gt, lt
  Comparator comparator_3 (.a(Operand1), .b(8'h3), .eq(comparator_3_eq));  // open: gt, lt
  Comparator comparator_4 (.a(Operand1), .b(8'h4), .eq(comparator_4_eq));  // open: gt, lt
  Comparator comparator_5 (.a(Operand1), .b(8'h5), .eq(comparator_5_eq));  // open: gt, lt
  and and_1 (isADDA, isADD, comparator_1_eq);
  and and_2 (isADDB, isADD, comparator_2_eq);
  and and_3 (isADDC, isADD, comparator_3_eq);
  and and_4 (isADDD, isADD, comparator_4_eq);
  and and_5 (isADDE, isADD, comparator_5_eq);
endmodule

module RegEnabledDecoder (
  input  isMOV,
  input  isADD,
  input  isSUB,
  input  isMUL,
  input  isDIV,
  input  isLOAD,
  input  isSTORE,
  input  [7:0] Operand1,
  output RegAEnabled,
  output RegBEnabled,
  output RegCEnabled,
  output RegDEnabled,
  output RegEEnabled
);

  wire isADDA, isADDB, isADDC, isADDD, isADDE, isDIVA, isDIVB, isDIVC, isDIVD, isDIVE, isLOADA, isLOADB,
       isLOADC, isLOADD, isLOADE, isMOVA, isMOVB, isMOVC, isMOVD, isMOVE, isMULA, isMULB, isMULC, isMULD,
       isMULE, isSTOREA, isSTOREB, isSTOREC, isSTORED, isSTOREE, isSUBA, isSUBB, isSUBC, isSUBD, isSUBE,
       or_1_out, or_2_out, or_3_out, or_4_out, or_5_out, or_6_out, or_7_out, or_8_out, or_9_out, or_10_out,
       or_11_out, or_12_out, or_13_out, or_14_out, or_15_out, or_16_out, or_17_out, or_18_out, or_19_out,
       or_20_out, or_21_out, or_22_out, or_23_out, or_24_out, or_29_out;

  ADDRegDecoder addregdecoder_1 (
    .isADD(isADD), .Operand1(Operand1), .isADDA(isADDA), .isADDB(isADDB), .isADDC(isADDC), .isADDD(isADDD),
    .isADDE(isADDE));
  SUBRegDecoder subregdecoder_1 (
    .isSUB(isSUB), .Operand1(Operand1), .isSUBA(isSUBA), .isSUBB(isSUBB), .isSUBC(isSUBC), .isSUBD(isSUBD),
    .isSUBE(isSUBE));
  STORERegDecoder storeregdecoder_1 (
    .isSTORE(isSTORE), .Operand1(Operand1), .isSTOREA(isSTOREA), .isSTOREB(isSTOREB), .isSTOREC(isSTOREC),
    .isSTORED(isSTORED), .isSTOREE(isSTOREE));
  MOVRegDecoder movregdecoder_1 (
    .isMOV(isMOV), .Operand1(Operand1), .isMOVA(isMOVA), .isMOVB(isMOVB), .isMOVC(isMOVC), .isMOVD(isMOVD),
    .isMOVE(isMOVE));
  MULRegDecoder mulregdecoder_1 (
    .isMUL(isMUL), .Operand1(Operand1), .isMULA(isMULA), .isMULB(isMULB), .isMULC(isMULC), .isMULD(isMULD),
    .isMULE(isMULE));
  DIVRegDecoder divregdecoder_1 (
    .isDIV(isDIV), .Operand1(Operand1), .isDIVA(isDIVA), .isDIVB(isDIVB), .isDIVC(isDIVC), .isDIVD(isDIVD),
    .isDIVE(isDIVE));
  LOADRegDecoder loadregdecoder_1 (
    .isLOAD(isLOAD), .Operand1(Operand1), .isLOADA(isLOADA), .isLOADB(isLOADB), .isLOADC(isLOADC),
    .isLOADD(isLOADD), .isLOADE(isLOADE));
  or or_1 (or_1_out, isADDA, isMOVA);
  or or_2 (or_2_out, isADDB, isMOVB);
  or or_3 (or_3_out, isADDC, isMOVC);
  or or_4 (or_4_out, isADDD, isMOVD);
  or or_5 (or_5_out, isADDE, isMOVE);
  or or_6 (or_6_out, or_1_out, isSUBA);
  or or_7 (or_7_out, or_2_out, isSUBB);
  or or_8 (or_8_out, or_3_out, isSUBC);
  or or_9 (or_9_out, or_4_out, isSUBD);
  or or_10 (or_10_out, or_5_out, isSUBE);
  or or_11 (or_11_out, or_6_out, isMULA);
  or or_12 (or_12_out, or_7_out, isMULB);
  or or_13 (or_13_out, or_8_out, isMULC);
  or or_14 (or_14_out, or_9_out, isMULD);
  or or_15 (or_15_out, or_10_out, isMULE);
  or or_16 (or_16_out, or_11_out, isDIVA);
  or or_17 (or_17_out, or_16_out, isLOADA);
  or or_18 (or_18_out, or_12_out, isDIVB);
  or or_19 (or_19_out, or_18_out, isLOADB);
  or or_20 (or_20_out, or_13_out, isDIVC);
  or or_21 (or_21_out, or_20_out, isLOADC);
  or or_22 (or_22_out, or_14_out, isDIVD);
  or or_23 (or_23_out, or_22_out, isLOADD);
  or or_24 (or_24_out, or_15_out, isDIVE);
  or or_25 (RegAEnabled, or_17_out, isSTOREA);
  or or_26 (RegBEnabled, or_19_out, isSTOREB);
  or or_27 (RegCEnabled, or_21_out, isSTOREC);
  or or_28 (RegDEnabled, or_23_out, isSTORED);
  or or_29 (or_29_out, or_24_out, isLOADE);
  or or_30 (RegEEnabled, or_29_out, isSTOREE);
endmodule

module SUBRegDecoder (
  input  isSUB,
  input  [7:0] Operand1,
  output isSUBA,
  output isSUBB,
  output isSUBC,
  output isSUBD,
  output isSUBE
);

  wire comparator_1_eq, comparator_2_eq, comparator_3_eq, comparator_4_eq, comparator_5_eq;

  Comparator comparator_1 (.a(Operand1), .b(8'h1), .eq(comparator_1_eq));  // open: gt, lt
  Comparator comparator_2 (.a(Operand1), .b(8'h2), .eq(comparator_2_eq));  // open: gt, lt
  Comparator comparator_3 (.a(Operand1), .b(8'h3), .eq(comparator_3_eq));  // open: gt, lt
  Comparator comparator_4 (.a(Operand1), .b(8'h4), .eq(comparator_4_eq));  // open: gt, lt
  Comparator comparator_5 (.a(Operand1), .b(8'h5), .eq(comparator_5_eq));  // open: gt, lt
  and and_1 (isSUBA, isSUB, comparator_1_eq);
  and and_2 (isSUBB, isSUB, comparator_2_eq);
  and and_3 (isSUBC, isSUB, comparator_3_eq);
  and and_4 (isSUBD, isSUB, comparator_4_eq);
  and and_5 (isSUBE, isSUB, comparator_5_eq);
endmodule

module MULRegDecoder (
  input  isMUL,
  input  [7:0] Operand1,
  output isMULA,
  output isMULB,
  output isMULC,
  output isMULD,
  output isMULE
);

  wire comparator_1_eq, comparator_2_eq, comparator_3_eq, comparator_4_eq, comparator_5_eq;

  Comparator comparator_1 (.a(Operand1), .b(8'h1), .eq(comparator_1_eq));  // open: gt, lt
  Comparator comparator_2 (.a(Operand1), .b(8'h2), .eq(comparator_2_eq));  // open: gt, lt
  Comparator comparator_3 (.a(Operand1), .b(8'h3), .eq(comparator_3_eq));  // open: gt, lt
  Comparator comparator_4 (.a(Operand1), .b(8'h4), .eq(comparator_4_eq));  // open: gt, lt
  Comparator comparator_5 (.a(Operand1), .b(8'h5), .eq(comparator_5_eq));  // open: gt, lt
  and and_1 (isMULA, isMUL, comparator_1_eq);
  and and_2 (isMULB, isMUL, comparator_2_eq);
  and and_3 (isMULC, isMUL, comparator_3_eq);
  and and_4 (isMULD, isMUL, comparator_4_eq);
  and and_5 (isMULE, isMUL, comparator_5_eq);
endmodule

module DIVRegDecoder (
  input  isDIV,
  input  [7:0] Operand1,
  output isDIVA,
  output isDIVB,
  output isDIVC,
  output isDIVD,
  output isDIVE
);

  wire comparator_1_eq, comparator_2_eq, comparator_3_eq, comparator_4_eq, comparator_5_eq;

  Comparator comparator_1 (.a(Operand1), .b(8'h1), .eq(comparator_1_eq));  // open: gt, lt
  Comparator comparator_2 (.a(Operand1), .b(8'h2), .eq(comparator_2_eq));  // open: gt, lt
  Comparator comparator_3 (.a(Operand1), .b(8'h3), .eq(comparator_3_eq));  // open: gt, lt
  Comparator comparator_4 (.a(Operand1), .b(8'h4), .eq(comparator_4_eq));  // open: gt, lt
  Comparator comparator_5 (.a(Operand1), .b(8'h5), .eq(comparator_5_eq));  // open: gt, lt
  and and_1 (isDIVA, isDIV, comparator_1_eq);
  and and_2 (isDIVB, isDIV, comparator_2_eq);
  and and_3 (isDIVC, isDIV, comparator_3_eq);
  and and_4 (isDIVD, isDIV, comparator_4_eq);
  and and_5 (isDIVE, isDIV, comparator_5_eq);
endmodule

module LOADRegDecoder (
  input  isLOAD,
  input  [7:0] Operand1,
  output isLOADA,
  output isLOADB,
  output isLOADC,
  output isLOADD,
  output isLOADE
);

  wire comparator_1_eq, comparator_2_eq, comparator_3_eq, comparator_4_eq, comparator_5_eq;

  Comparator comparator_1 (.a(Operand1), .b(8'h1), .eq(comparator_1_eq));  // open: gt, lt
  Comparator comparator_2 (.a(Operand1), .b(8'h2), .eq(comparator_2_eq));  // open: gt, lt
  Comparator comparator_3 (.a(Operand1), .b(8'h3), .eq(comparator_3_eq));  // open: gt, lt
  Comparator comparator_4 (.a(Operand1), .b(8'h4), .eq(comparator_4_eq));  // open: gt, lt
  Comparator comparator_5 (.a(Operand1), .b(8'h5), .eq(comparator_5_eq));  // open: gt, lt
  and and_1 (isLOADA, isLOAD, comparator_1_eq);
  and and_2 (isLOADB, isLOAD, comparator_2_eq);
  and and_3 (isLOADC, isLOAD, comparator_3_eq);
  and and_4 (isLOADD, isLOAD, comparator_4_eq);
  and and_5 (isLOADE, isLOAD, comparator_5_eq);
endmodule

module STORERegDecoder (
  input  isSTORE,
  input  [7:0] Operand1,
  output isSTOREA,
  output isSTOREB,
  output isSTOREC,
  output isSTORED,
  output isSTOREE
);

  wire comparator_1_eq, comparator_2_eq, comparator_3_eq, comparator_4_eq, comparator_5_eq;

  Comparator comparator_1 (.a(Operand1), .b(8'h1), .eq(comparator_1_eq));  // open: gt, lt
  Comparator comparator_2 (.a(Operand1), .b(8'h2), .eq(comparator_2_eq));  // open: gt, lt
  Comparator comparator_3 (.a(Operand1), .b(8'h3), .eq(comparator_3_eq));  // open: gt, lt
  Comparator comparator_4 (.a(Operand1), .b(8'h4), .eq(comparator_4_eq));  // open: gt, lt
  Comparator comparator_5 (.a(Operand1), .b(8'h5), .eq(comparator_5_eq));  // open: gt, lt
  and and_1 (isSTOREA, isSTORE, comparator_1_eq);
  and and_2 (isSTOREB, isSTORE, comparator_2_eq);
  and and_3 (isSTOREC, isSTORE, comparator_3_eq);
  and and_4 (isSTORED, isSTORE, comparator_4_eq);
  and and_5 (isSTOREE, isSTORE, comparator_5_eq);
endmodule
